# Fritzing sketch Shield (saved by Fritzing 0.9.3b)
perfboards: 2

parts:
  U1 = RF-LINK_TX [package=rf-link_tx]
  U2 = RF-LINK_RX [package=rf-link_rx]
  Q1 = TRANSISTOR_NPN [part_number=2N2222 package=to-92]
  R1 = Resistor [tolerance=±5% resistance=470 package=THT]
  IR1 = TSOP312.., 314.. [package=THT]
  D1 = LTE-302 [part_number="IR LED" package=lte-302]
  J1 = screw terminal, 4 pins
  Part1 = Logic Level Converter
  J2 = screw terminal, 4 pins
  J3 = screw terminal, 4 pins
  J4 = screw terminal, 4 pins
  Raspberry_Pi2 = Raspberry Pi 2
  Part2 = Arduino Uno (Rev3)
  LED2 = smd LED [color="Red (633nm)" package="1206 [SMD]"]
  R6 = Resistor [tolerance=±5% resistance=220 package="2010 [SMD]"]
  J5 = screw terminal, 4 pins
  R4 = Resistor [tolerance=±5% resistance=1k package="2010 [SMD]"]
  R3 = Resistor [tolerance=±5% resistance=10k package="2010 [SMD]"]

nets:
  N1: U1.ANT, Q1.E, IR1.GND, J1.pin3
  N2: U1.+5V, Part2.D7
  N3: U2.Data#2, Part2.D3_PWM
  N4: Q1.B, R1.Pin_0
  N5: Q1.C, D1.C, J1.pin2
  N6: R1.Pin_1, Part2.D9_PWM
  N7: IR1.Vs, D1.A, J1.pin1, Part1.HV, J3.pin2
  N8: IR1.Data, J1.pin4, Part2.D2
  N9: Part1.GND, J3.pin1, J4.pin3
  N10: Part1.LV, Raspberry_Pi2.3v3
  N11: Part1.TX_HV, J2.pin3, J3.pin4, Part2.D1/TX
  N12: Part1.RX_HV, J2.pin4, J3.pin3, Part2.D0/RX
  N13: J2.pin1, Part2.A5/SCL
  N14: J2.pin2, Part2.A4/SDA
  N15: Raspberry_Pi2.GPIO2, J5.pin4
  N16: Raspberry_Pi2.GPIO3, J5.pin3
  N17: Raspberry_Pi2.GPIO21, R4.Pin_0
  N18: Raspberry_Pi2.GPIO16, LED2.cathode
  N19: LED2.anode, R6.Pin_1
  N20: R6.Pin_0, R3.Pin_1
  N21: J5.pin2, R4.Pin_1, R3.Pin_0

notes:
  SDA i SCL
  interrupt

custom parts:
  RF-LINK_RX: RF Link receivers- WRL-8947, 8948, 8949, 8950
